# Fritzing sketch Growthline 1_1 (saved by Fritzing 0.9.3b)
circuit board: 8.46667cm x 5.64444cm
breadboards: 1

parts:
  Part1 = Adafruit TSL2561 [part_number="Adafruit #439"]
  Part2 = Adafruit 2.8 inch Captouch TFT [part_number="Adafruit #2090"]
  RHT1 = Humidity and Temperature Sensor RHT03
  Part3 = SHT1x-Breakout
  pH_Circuit1 = pH Circuit
  Pre-Assembled_Female_BNC1 = Pre-Assembled Female BNC
  Arduino_Uno = Arduino Uno (Rev3)

nets:
  GND: Part1.GND, Part2.GND, RHT1.GND_1, RHT1.GND_2, Part3.GND, pH_Circuit1.GND#0, Arduino_Uno.GND
  3.3V: Part1.3.3V, Part2.3.3V, Arduino_Uno.3V3
  N1: Part1.SDA, Part2.SDA, Arduino_Uno.A4/SDA
  N2: Part1.SCL, Part2.SCL, Arduino_Uno.A5/SCL
  N3: Part2.C/D_CLK, Arduino_Uno.D13/SCK
  N4: Part2.MISO, Arduino_Uno.D12/MISO
  N5: Part2.MOSI, Arduino_Uno.D11_PWM/MOSI
  N6: Part2.CS, Arduino_Uno.D10_PWM/SS
  N7: Part2.D/C_WR, Arduino_Uno.D9_PWM
  N8: Part2.SD_CS, Arduino_Uno.D4
  VCC: RHT1.Vcc, Part3.VCC, pH_Circuit1.Vcc, Pre-Assembled_Female_BNC1.NC, Arduino_Uno.5V
  N9: RHT1.Data-signal, Arduino_Uno.D5_PWM
  N10: Part3.SCK, Arduino_Uno.D7
  N11: Part3.DATA, Arduino_Uno.D6_PWM
  N12: pH_Circuit1.TX, Arduino_Uno.D2
  N13: pH_Circuit1.RX, Arduino_Uno.D3_PWM
  N14: pH_Circuit1.PRB, Pre-Assembled_Female_BNC1.PRB
  N15: pH_Circuit1.GND#5, Pre-Assembled_Female_BNC1.GND

custom parts:
  Adafruit TSL2561: The TSL2561 luminosity sensor is an advanced digital light sensor, ideal for use in a wide range of light situations. Compared to low cost CdS cells, this sensor is more precise, allowing for exact lux calculations and can be configured for different gain/timing ranges to detect light ranges from up to 0.1 - 40,000+ Lux on the fly. The best part of this sensor is that it contains both infrared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
  Adafruit 2.8 inch Captouch TFT: Add some jazz & pizazz to your project with a color capactive touchscreen LCD. This TFT display is big (2.8" diagonal) bright (4 white-LED backlight) and colorful! 240x320 pixels with individual RGB pixel control, this has way more resolution than a black and white 128x64 display. As a bonus, this display has a capacitive single-touch touchscreen attached to it already, so you can detect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
